// Logisim project reo1_logisim_portas_logicas_layra.circ as structural Verilog: 1 circuit, main circuit main
// C
module main (
  input  A,
  input  B,
  input  B_2,
  input  C,
  input  A_2,
  input  B_3,
  input  C_2,
  input  D,
  output X,
  output X_2
);

  wire nand_1_out, nand_2_out, nand_3_out, nor_1_out, nor_2_out, nor_3_out, nor_4_out, nor_5_out, nor_6_out;

  nand nand_1 (nand_1_out, A, B);
  nand nand_2 (nand_2_out, C, C);
  nor nor_1 (nor_1_out, A_2, A_2);
  nor nor_2 (nor_2_out, B_3, B_3);
  nor nor_3 (nor_3_out, C_2, C_2);
  nor nor_4 (nor_4_out, D, D);
  nand nand_3 (nand_3_out, B_2, nand_2_out);
  nor nor_5 (nor_5_out, nor_2_out, nor_3_out);
  nand nand_4 (X, nand_1_out, nand_3_out);
  nor nor_6 (nor_6_out, nor_1_out, nor_5_out);
  nor nor_7 (X_2, nor_6_out, nor_4_out);

  // Notes on the sheet:
  //   1.
  //   2.
  //   __
  //   AB
  //   B
  //   _
  //   C
  //   _
  //   A
  //   _
  //   B
  //   _
  //   C
  //   _
  //   D
  //   _
  //   BC
  //   _
  //   _
  //   B+C
  //   _
  //   _
  //   _
  //   A+B+C
endmodule
