// Logisim project circuito letra C.circ as structural Verilog: 1 circuit, main circuit main
module main (
  input  in_1,
  input  in_2,
  input  in_3,
  input  in_4,
  output out_5,
  output out_6,
  output out_7,
  output out_8
);

  wire adder_1_cout, and_2_out, and_3_out, and_4_out;

  and and_1 (out_5, in_1, in_1, in_3);
  and and_2 (and_2_out, in_2, in_2, in_3);
  and and_3 (and_3_out, in_1, in_1, in_4);
  and and_4 (and_4_out, in_2, in_4);
  Adder #(.width(1)) adder_1 (.a(and_2_out), .b(and_3_out), .out(out_6), .cin(1'b0), .cout(adder_1_cout));
  Adder #(.width(1)) adder_2 (.a(adder_1_cout), .b(and_4_out), .out(out_7), .cin(1'b0), .cout(out_8));
endmodule
