// Logisim project circuitos letra A.circ as structural Verilog: 1 circuit, main circuit main
module main (
  input  _2_1,
  input  _2_2,
  input  in_3,
  input  in_4,
  input  in_5,
  input  in_6,
  input  in_7,
  input  in_8,
  input  in_9,
  input  in_10,
  input  in_11,
  input  in_12,
  input  _2_5,
  input  in_14,
  input  in_15,
  output out_16,
  output out_17,
  output out_18,
  output out_19
);

  wire and_1_out, nand_1_out, nor_1_out, not_1_out, not_2_out, not_3_out, not_4_out, not_5_out, or_1_out;

  nand nand_1 (nand_1_out, in_7, in_7);
  nor nor_1 (nor_1_out, in_10, in_12);
  nand nand_2 (out_19, _2_5, in_14, in_15);
  and and_1 (and_1_out, nand_1_out, nor_1_out);
  nand nand_3 (out_17, and_1_out, and_1_out);
  not not_1 (not_1_out, _2_2);
  not not_2 (not_2_out, in_8);
  not not_3 (not_3_out, in_9);
  not not_4 (not_4_out, in_11);
  or or_1 (or_1_out, in_4, in_6);
  not not_5 (not_5_out, or_1_out);
  or or_2 (out_18, not_2_out, not_3_out, not_4_out);
  and and_2 (out_16, not_1_out, not_5_out);

  // Notes on the sheet:
  //   2.3
  //   2.4
endmodule
