// Logisim project circuitos letra B.circ as structural Verilog: 1 circuit, main circuit main
module main (
  input  _2_1,
  input  _2_2,
  input  in_3,
  input  in_4,
  input  in_5,
  input  in_6,
  input  in_7,
  input  in_8,
  input  in_9,
  input  A,
  input  B,
  input  C,
  input  D,
  input  in_14,
  input  in_15,
  input  in_16,
  input  A_2,
  input  B_2,
  input  C_2,
  input  D_2,
  output out_21,
  output out_22,
  output out_23,
  output out_24,
  output out_25
);

  wire and_1_out, and_4_out, and_5_out, and_6_out, and_7_out, nand_1_out, nand_2_out, nand_3_out, not_1_out,
       not_2_out, not_3_out, not_4_out, not_5_out;

  not not_1 (not_1_out, and_1_out);
  and and_1 (and_1_out, in_3, in_5);
  nand nand_1 (nand_1_out, in_14, in_15);
  nand nand_2 (nand_2_out, in_9, nand_1_out, in_16);
  and and_2 (out_21, _2_1, not_1_out, in_7);
  nand nand_3 (nand_3_out, B_2, C_2);
  nand nand_4 (out_24, nand_2_out, nand_2_out);
  and and_3 (out_25, nand_3_out, A_2, D_2);
  not not_2 (not_2_out, in_4);
  not not_3 (not_3_out, in_6);
  and and_4 (and_4_out, _2_2, not_2_out);
  and and_5 (and_5_out, not_3_out, in_8);
  not not_4 (not_4_out, C);
  and and_6 (and_6_out, A, not_4_out, D);
  not not_5 (not_5_out, B);
  and and_7 (and_7_out, A, not_5_out, D);
  or or_1 (out_22, and_4_out, and_5_out);
  or or_2 (out_23, and_6_out, and_7_out);

  // Notes on the sheet:
  //   2.3
  //   2.5
  //   2.4
endmodule
