// Logisim project circuitoReo4-layra.circ as structural Verilog: 5 circuits, main circuit main
module main (
  input  D,
  input  C,
  input  in_3,
  input  B,
  input  A
);

  wire driver_bcd_7seg_1_s_mux1, driver_bcd_7seg_1_s_mux2, driver_bcd_7seg_1_s_mux3,
       driver_bcd_7seg_1_s_mux4, driver_bcd_7seg_1_s_mux5, driver_bcd_7seg_1_s_mux6,
       driver_bcd_7seg_1_s_mux7, not_1_out, \x_espera_1_saída_x ;

  X__Espera x_espera_1 (.A(A), .B(B), .C(C), .D(D), .\Saída_X (\x_espera_1_saída_x ));
  not not_1 (not_1_out, \x_espera_1_saída_x );
  LED led_1 (.in(\x_espera_1_saída_x ));
  Driver_BCD_7seg driver_bcd_7seg_1 (
    .D(D), .C(C), .B(B), .A(A), .Enable(not_1_out), .S_MUX1(driver_bcd_7seg_1_s_mux1),
    .S_MUX2(driver_bcd_7seg_1_s_mux2), .S_MUX3(driver_bcd_7seg_1_s_mux3), .S_MUX4(driver_bcd_7seg_1_s_mux4),
    .S_MUX5(driver_bcd_7seg_1_s_mux5), .S_MUX6(driver_bcd_7seg_1_s_mux6), .S_MUX7(driver_bcd_7seg_1_s_mux7));
  _7_Segment_Display u_7_segment_display_1 (
    .g(driver_bcd_7seg_1_s_mux1), .f(driver_bcd_7seg_1_s_mux2), .a(driver_bcd_7seg_1_s_mux3),
    .b(driver_bcd_7seg_1_s_mux4), .e(driver_bcd_7seg_1_s_mux5), .d(driver_bcd_7seg_1_s_mux6),
    .c(driver_bcd_7seg_1_s_mux7), .dp(in_3));

  // Notes on the sheet:
  //   Espera
endmodule

module X__Espera (
  input  A,
  input  B,
  input  C,
  input  D,
  output \Saída_X 
);

  wire and_1_out, and_2_out, not_1_out, not_2_out, not_3_out, not_4_out, not_5_out;

  not not_1 (not_1_out, A);
  not not_2 (not_2_out, B);
  not not_3 (not_3_out, C);
  not not_4 (not_4_out, B);
  not not_5 (not_5_out, D);
  and and_1 (and_1_out, not_1_out, not_2_out, not_3_out);
  and and_2 (and_2_out, not_4_out, C, not_5_out);
  or or_1 (\Saída_X , and_1_out, and_2_out);
  LED led_1 (.in(\Saída_X ));
endmodule

module Y__Economia (
  input  A,
  input  B,
  input  C,
  input  D,
  output \Saída_Y 
);

  wire and_1_out, and_2_out, not_1_out, not_2_out;

  not not_1 (not_1_out, C);
  not not_2 (not_2_out, B);
  and and_1 (and_1_out, B, not_1_out);
  and and_2 (and_2_out, not_2_out, C, D);
  LED led_1 (.in(\Saída_Y ));
  or or_1 (\Saída_Y , and_1_out, and_2_out);
endmodule

module Z__Desempenho (
  input  A,
  input  B,
  input  C,
  input  D,
  output \Saída_Z 
);

  wire and_1_out, and_2_out, not_1_out, not_2_out;

  not not_1 (not_1_out, B);
  not not_2 (not_2_out, C);
  and and_1 (and_1_out, B, C);
  and and_2 (and_2_out, A, not_1_out, not_2_out);
  LED led_1 (.in(\Saída_Z ));
  or or_1 (\Saída_Z , and_1_out, and_2_out);
endmodule

module Driver_BCD_7seg (
  input  D,
  input  C,
  input  B,
  input  A,
  input  Enable,
  output S_MUX1,
  output S_MUX2,
  output S_MUX3,
  output S_MUX4,
  output S_MUX5,
  output S_MUX6,
  output S_MUX7
);

  Multiplexer #(.select(4)) multiplexer_1 (
    .in0(1'b0), .in1(1'b0), .in2(1'b1), .in3(1'b1), .in4(1'b1), .in5(1'b1), .in6(1'b1), .in7(1'b0),
    .in8(1'b1), .in9(1'b1), .in10(1'b1), .in11(1'b1), .in12(1'b1), .in13(1'b1), .in14(1'b1), .in15(1'b0),
    .out(S_MUX1), .sel({A, B, C, D}), .en(Enable));
  Multiplexer #(.select(4)) multiplexer_2 (
    .in0(1'b1), .in1(1'b0), .in2(1'b1), .in3(1'b0), .in4(1'b0), .in5(1'b0), .in6(1'b1), .in7(1'b0),
    .in8(1'b1), .in9(1'b0), .in10(1'b1), .in11(1'b0), .in12(1'b0), .in13(1'b0), .in14(1'b1), .in15(1'b0),
    .out(S_MUX5), .sel({A, B, C, D}), .en(Enable));
  Multiplexer #(.select(4)) multiplexer_3 (
    .in0(1'b1), .in1(1'b0), .in2(1'b0), .in3(1'b0), .in4(1'b1), .in5(1'b1), .in6(1'b1), .in7(1'b0),
    .in8(1'b1), .in9(1'b1), .in10(1'b0), .in11(1'b0), .in12(1'b1), .in13(1'b1), .in14(1'b1), .in15(1'b0),
    .out(S_MUX2), .sel({A, B, C, D}), .en(Enable));
  Multiplexer #(.select(4)) multiplexer_4 (
    .in0(1'b1), .in1(1'b0), .in2(1'b1), .in3(1'b1), .in4(1'b0), .in5(1'b1), .in6(1'b1), .in7(1'b0),
    .in8(1'b1), .in9(1'b1), .in10(1'b1), .in11(1'b1), .in12(1'b0), .in13(1'b1), .in14(1'b1), .in15(1'b0),
    .out(S_MUX6), .sel({A, B, C, D}), .en(Enable));
  Multiplexer #(.select(4)) multiplexer_5 (
    .in0(1'b1), .in1(1'b0), .in2(1'b1), .in3(1'b1), .in4(1'b0), .in5(1'b1), .in6(1'b1), .in7(1'b1),
    .in8(1'b1), .in9(1'b1), .in10(1'b0), .in11(1'b0), .in12(1'b0), .in13(1'b1), .in14(1'b0), .in15(1'b0),
    .out(S_MUX3), .sel({A, B, C, D}), .en(Enable));
  Multiplexer #(.select(4)) multiplexer_6 (
    .in0(1'b1), .in1(1'b1), .in2(1'b0), .in3(1'b1), .in4(1'b1), .in5(1'b1), .in6(1'b1), .in7(1'b1),
    .in8(1'b1), .in9(1'b1), .in10(1'b0), .in11(1'b1), .in12(1'b0), .in13(1'b0), .in14(1'b0), .in15(1'b0),
    .out(S_MUX7), .sel({A, B, C, D}), .en(Enable));
  Multiplexer #(.select(4)) multiplexer_7 (
    .in0(1'b1), .in1(1'b1), .in2(1'b1), .in3(1'b1), .in4(1'b1), .in5(1'b0), .in6(1'b0), .in7(1'b1),
    .in8(1'b1), .in9(1'b1), .in10(1'b0), .in11(1'b0), .in12(1'b1), .in13(1'b0), .in14(1'b0), .in15(1'b0),
    .out(S_MUX4), .sel({A, B, C, D}), .en(Enable));
endmodule
