// Logisim project atividade-reo5-layra.circ as structural Verilog: 4 circuits, main circuit main
module main (
  input  SOMA_SUB,
  input  A3,
  input  A2,
  input  A1,
  input  A0,
  input  B3,
  input  B2,
  input  B1,
  input  B0,
  output OVERFLOW,
  output PARIDADE,
  output S3,
  output S2,
  output S1,
  output S0
);

  wire xor_1_out, xor_2_out, xor_3_out, xor_4_out;

  xor xor_1 (xor_1_out, B3, SOMA_SUB);
  xor xor_2 (xor_2_out, B2, SOMA_SUB);
  xor xor_3 (xor_3_out, B1, SOMA_SUB);
  xor xor_4 (xor_4_out, B0, SOMA_SUB);
  somador_paralelo somador_paralelo_1 (
    .A3(A3), .A2(A2), .A1(A1), .A0(A0), .B3(xor_1_out), .B2(xor_2_out), .B1(xor_3_out), .B0(xor_4_out),
    .OVERFLOW(OVERFLOW), .S3(S3), .S2(S2), .S1(S1), .S0(S0), .Cin(SOMA_SUB));
  gerador_de_paridade gerador_de_paridade_1 (.s3(S3), .s2(S2), .s1(S1), .s0(S0), .paridade(PARIDADE));
endmodule

module somador_completo (
  input  A,
  input  B,
  input  Cin,
  output S,
  output Cout
);

  wire and_1_out, and_2_out, and_3_out, xor_1_out;

  xor xor_1 (xor_1_out, A, B);
  and and_1 (and_1_out, B, Cin);
  and and_2 (and_2_out, Cin, A);
  and and_3 (and_3_out, B, A);
  xor xor_2 (S, xor_1_out, Cin);
  or or_1 (Cout, and_1_out, and_2_out, and_3_out);
endmodule

module somador_paralelo (
  input  A3,
  input  A2,
  input  A1,
  input  A0,
  input  B3,
  input  B2,
  input  B1,
  input  B0,
  input  Cin,
  output OVERFLOW,
  output S3,
  output S2,
  output S1,
  output S0
);

  wire somador_completo_2_cout, somador_completo_3_cout, somador_completo_4_cout;

  somador_completo somador_completo_1 (.A(A3), .B(B3), .Cin(somador_completo_2_cout), .S(S3), .Cout(OVERFLOW));
  somador_completo somador_completo_2 (
    .A(A2), .B(B2), .Cin(somador_completo_3_cout), .S(S2), .Cout(somador_completo_2_cout));
  somador_completo somador_completo_3 (
    .A(A1), .B(B1), .Cin(somador_completo_4_cout), .S(S1), .Cout(somador_completo_3_cout));
  somador_completo somador_completo_4 (.A(A0), .B(B0), .Cin(Cin), .S(S0), .Cout(somador_completo_4_cout));
endmodule

module gerador_de_paridade (
  input  s3,
  input  s2,
  input  s1,
  input  s0,
  output paridade
);

  wire xor_1_out, xor_2_out;

  xor xor_1 (xor_1_out, s0, s1);
  xor xor_2 (xor_2_out, xor_1_out, s2);
  xor xor_3 (paridade, xor_2_out, s3);
endmodule
